// Digital circuit main.dig as structural Verilog
module main (
  input  clk,
  input  reset,
  input  [7:0] kb_data,
  input  [12:0] disp_read,
  input  kb_en,
  output [31:0] WB_MUX,
  output [31:0] DISP
);

  wire ctrl_bank_en, ctrl_branch_en, ctrl_enc, ctrl_flags_we, ctrl_jump_type, ctrl_mem_rd, ctrl_mem_wr,
       ctrl_mul_div_en, ctrl_pc_link_WE, ctrl_reg_we, ctrl_shift_op, HALT_IN, mem_rd_out, mul_nxt_enc,
       nflag_A_zero, reg_a, reg_c, seq_exec, seq_fetch, shift_mul_p_enc;
  wire [1:0] ctrl_cycles, ctrl_sp_out;
  wire [2:0] ctrl_bus_sel, ctrl_pc_src, ctrl_wb_sel;
  wire [3:0] BANK_SEL, ctrl_byte_sel, ctrl_ir_sel, ctrl_pc_cond;
  wire [5:0] ctrl_alu_pre, ir_addr_a, ir_addr_b, ir_addr_w;
  wire [7:0] ctrl_alu_op;
  wire [9:0] ir_opcode;
  wire [12:0] csr_flags;
  wire [21:0] IR_ADDR, ir_offset;
  wire [23:0] mem_addr, pc_link, pc_out, pc_save, sp_out;
  wire [31:0] alu_out, ir_bus, mem_din, mem_ram_out, reg_b;

  alu_control alu_control_1 (.op(ir_opcode), .alu_op(ctrl_alu_op), .alu_pre(ctrl_alu_pre), .flag_we(ctrl_flags_we));
  ir_reg_control ir_reg_control_1 (
    .op(ir_opcode), .ir_imm_sel(ctrl_ir_sel), .wb_sel(ctrl_wb_sel), .reg_we(ctrl_reg_we));
  mem_bus_control mem_bus_control_1 (.op(ir_opcode), .ctrl_bussel(ctrl_bus_sel));
  mem_io_control mem_io_control_1 (
    .op(ir_opcode), .bank_en(ctrl_bank_en), .mem_rd(ctrl_mem_rd), .mem_wr(ctrl_mem_wr),
    .byte_sel(ctrl_byte_sel));
  pc_control pc_control_1 (
    .op(ir_opcode), .exec(seq_exec), .branch_en(ctrl_branch_en), .jump_type(ctrl_jump_type),
    .pc_src(ctrl_pc_src), .pc_link_we(ctrl_pc_link_WE), .cycles(ctrl_cycles), .pc_cond(ctrl_pc_cond),
    .sp_out(ctrl_sp_out), .HALT_IN(HALT_IN));
  // shift_mul_control shift_mul_control_1: pin names not known; wires that end beside it: ir_opcode, ctrl_shift_op, ctrl_mul_div_en, ctrl_enc
  // alu_32b_final alu_32b_final_1: pin names not known; wires that end beside it: reg_a, ir_bus, reg_c, ctrl_alu_pre, ctrl_alu_op, clk, ctrl_flags_we, nflag_A_zero, alu_out, csr_flags
  // register register_1: pin names not known; wires that end beside it: ctrl_reg_we, WB_MUX, ir_addr_a, ir_addr_b, ir_addr_w, seq_exec, clk, BANK_SEL, ctrl_bank_en, reg_a, reg_b, reg_c
  // mul_div mul_div_1: pin names not known; wires that end beside it: ir_bus, ctrl_shift_op, ctrl_mul_div_en, reg_a, ctrl_enc, shift_mul_p_enc, nflag_A_zero, mul_nxt_enc
  vga vga_1 (.mem_addr(mem_addr), .mem_din(WB_MUX), .disp_read_addr(disp_read), .clk(clk), .disp_data_out(DISP));
  ir ir_1 (
    .DATA_IN(mem_din), .LOAD(seq_fetch), .CLK(clk), .ir_sel(ctrl_ir_sel), .RegB(reg_b), .OPCODE(ir_opcode),
    .ADDR_A(ir_addr_a), .ADDR_B(ir_addr_b), .ADDR_W(ir_addr_w), .ADDR_ABS(IR_ADDR), .OFFSET(ir_offset),
    .ir_imm_out(ir_bus), .BANK_SEL(BANK_SEL));
  RAMDualPort #(.AddrBits(8), .Bits(32)) ramdualport_1 (
    .A(mem_addr[7:0]), .Din(WB_MUX), .str(ctrl_mem_wr), .C(clk), .ld(mem_rd_out), .D(mem_ram_out));
  // byte_lane_decoder byte_lane_decoder_1: pin names not known; wires that end beside it: mem_ram_out, ctrl_byte_sel, kb_data, mem_din
  program_counter program_counter_1 (
    .mem_din(mem_din), .alu_in(alu_out), .pc_src(ctrl_pc_src), .OFFSET(ir_offset), .RESET(reset),
    .cycles(ctrl_cycles), .csr_flags(csr_flags), .pc_cond(ctrl_pc_cond), .jump_type(ctrl_jump_type),
    .branch_en(ctrl_branch_en), .INT_EN_IN(1'b1), .HALT_IN(HALT_IN), .INT_REQ(kb_en), .INT_VEC_0(1'b1),
    .INT_VEC_1(1'b1), .INT_VEC_2(1'b1), .link_in(ctrl_pc_link_WE), .clk(clk), .PC_OUT(pc_out),
    .PC_SAVE(pc_save), .FETCH(seq_fetch), .EXECUTE(seq_exec), .PC_LINK(pc_link));
  sp sp_1 (.sp_op(ctrl_sp_out), .CLK(clk), .Reset(reset), .sp_load_in(alu_out), .seq_exec(seq_exec), .sp_out(sp_out));
  // wb_mux wb_mux_1: pin names not known; wires that end beside it: ctrl_wb_sel, alu_out, shift_mul_p_enc, pc_save, mem_din, reg_a, ir_bus, csr_flags, mul_nxt_enc, WB_MUX
  bus_arbitration bus_arbitration_1 (
    .FETCH(seq_fetch), .IR_ADDR(IR_ADDR), .MEM_RD_IN(ctrl_mem_rd), .addr_sel(ctrl_bus_sel), .Reg_b(reg_b),
    .Pc_out(pc_out), .SP_out(sp_out), .Alu_in(alu_out), .ADDR_BUS(mem_addr), .MEM_RD_OUT(mem_rd_out));

  // Other names for the same wires on the sheet: disp_out[31:0] = DISP; disp_read_addr[12:0] = disp_read;
  //   wb_data[31:0] = WB_MUX

  // Notes on the sheet:
  //   Control Unit
  //   ALU
  //   Shift - Encoder
  //   Memory
  //   Instruction Register
  //   Program Counter
  //   Data Bus Switch
endmodule
